# Fritzing sketch sensor (saved by Fritzing 0.9.3b)
circuit board: 6.23374cm x 3.22781cm
breadboards: 1

parts:
  Raspberry_Pi_1 = Raspberry Pi 3 [part_number=RPI-3-V1.2]
  JP1 = M16 [package=1x16_machine-pin-header_lock.004]

nets:
  3V3: Raspberry_Pi_1.3v3, Raspberry_Pi_1.3V3, JP1.2, JP1.16
  N1: Raspberry_Pi_1.GPIO2, JP1.8, JP1.9
  N2: Raspberry_Pi_1.GPIO3, JP1.7
  N3: Raspberry_Pi_1.GND, JP1.1, JP1.4
